# Fritzing sketch Untitled Sketch (saved by Fritzing 0.9.3b)

parts:
  U2 = ESP8266 NodeMCU LoLin module
  M1 = DHT11-Grove-Temperature-Sensor_1
  hc-sr1 = hc-sr04
  LED1 = smd LED [color="Red (633nm)" package="0805 [SMD]"]
  J1 = Piezo Speaker
  YL-83_-_Control_Board3 = YL-83 Rain Sensor - Control Board
  YL-83_-_Detection_Board2 = YL-83 Rain Sensor - Detection Board
  LED2 = smd LED [color="Green (570nm)" package="0805 [SMD]"]
  Part1 = LCD1602-I2C

nets:
  N1: U2.D0, LED1.anode
  N2: U2.D1, hc-sr1.Trig
  N3: U2.D2, hc-sr1.Echo
  N4: U2.D3, M1.connector0
  N5: U2.D4, LED2.anode
  N6: U2.GND, M1.connector3
  N7: U2.D5, Part1.SDA
  N8: U2.D6, Part1.SCL
  N9: U2.Vin, M1.connector2
  N10: U2.A0, YL-83_-_Control_Board3.AO
  VCC: hc-sr1.VCC, Part1.VCC
  GND: hc-sr1.GND, Part1.GND
  N11: J1.pin1, YL-83_-_Control_Board3.GND
  N12: YL-83_-_Control_Board3.POS, YL-83_-_Detection_Board2.POS
  N13: YL-83_-_Control_Board3.NEG, YL-83_-_Detection_Board2.NEG

custom parts:
  ESP8266 NodeMCU LoLin module: ESP8266 based NodeMCU
  YL-83 Rain Sensor - Control Board: The YL-83 is a rain sensor that has more resistance when dry and less resistance when wet. The module runs at 5V.
  YL-83 Rain Sensor - Detection Board: The YL-83 is a rain sensor that has more resistance when dry and less resistance when wet. The module runs at 5V.
  LCD1602-I2C: A standard character display, usually with 2x16 characters. Comes in many colors with LCM1602 IIC attached.
